// Logisim project add_and_sub.circ as structural Verilog: 2 circuits, main circuit main
module main (
  input  [7:0] in_1,
  input  [7:0] in_2,
  input  [7:0] in_3,
  input  [7:0] in_4,
  input  in_5,
  input  [7:0] in_6,
  input  [7:0] in_7,
  input  [7:0] in_8,
  input  [7:0] in_9
);

  wire clock_1_out;
  wire [7:0] alu_1_vec3_1, alu_1_vec3_2, alu_1_vec3_3, alu_1_vec3_4, register_1_q, register_2_q,
       register_3_q, register_4_q, register_5_q, register_6_q, register_7_q, register_8_q;

  Register register_1 (.D(in_1), .clk(clock_1_out), .Q(register_1_q));  // open: en, clr
  Register register_2 (.D(in_2), .clk(clock_1_out), .Q(register_2_q));  // open: en, clr
  Register register_3 (.D(in_3), .clk(clock_1_out), .Q(register_3_q));  // open: en, clr
  Register register_4 (.D(in_4), .clk(clock_1_out), .Q(register_4_q));  // open: en, clr
  Register register_5 (.D(in_6), .clk(clock_1_out), .Q(register_5_q));  // open: en, clr
  Register register_6 (.D(in_7), .clk(clock_1_out), .Q(register_6_q));  // open: en, clr
  Register register_7 (.D(in_8), .clk(clock_1_out), .Q(register_7_q));  // open: en, clr
  Register register_8 (.D(in_9), .clk(clock_1_out), .Q(register_8_q));  // open: en, clr
  Clock clock_1 (.out(clock_1_out));
  alu alu_1 (
    .vec1_1(register_1_q), .vec1_2(register_2_q), .vec1_3(register_3_q), .vec1_4(register_4_q),
    .opcode(in_5), .vec2_1(register_5_q), .vec2_2(register_6_q), .vec2_3(register_7_q),
    .vec2_4(register_8_q), .vec3_4(alu_1_vec3_4), .vec3_3(alu_1_vec3_3), .vec3_2(alu_1_vec3_2),
    .vec3_1(alu_1_vec3_1));
  Register register_9 (.D(alu_1_vec3_1), .clk(clock_1_out));  // open: en, Q, clr
  Register register_10 (.D(alu_1_vec3_2), .clk(clock_1_out));  // open: en, Q, clr
  Register register_11 (.D(alu_1_vec3_3), .clk(clock_1_out));  // open: en, Q, clr
  Register register_12 (.D(alu_1_vec3_4), .clk(clock_1_out));  // open: en, Q, clr
endmodule

module alu (
  input  [7:0] vec1_1,
  input  [7:0] vec1_2,
  input  [7:0] vec1_3,
  input  [7:0] vec1_4,
  input  opcode,
  input  [7:0] vec2_1,
  input  [7:0] vec2_2,
  input  [7:0] vec2_3,
  input  [7:0] vec2_4,
  output [7:0] vec3_4,
  output [7:0] vec3_3,
  output [7:0] vec3_2,
  output [7:0] vec3_1
);

  wire [7:0] adder_1_out, adder_2_out, adder_3_out, adder_4_out, subtractor_1_out, subtractor_2_out,
       subtractor_3_out, subtractor_4_out;

  Adder adder_1 (.a(vec1_1), .b(vec2_1), .out(adder_1_out));  // open: cin, cout
  Subtractor subtractor_1 (.a(vec1_1), .b(vec2_1), .out(subtractor_1_out));  // open: bin, bout
  Adder adder_2 (.a(vec1_2), .b(vec2_2), .out(adder_2_out));  // open: cin, cout
  Subtractor subtractor_2 (.a(vec1_2), .b(vec2_2), .out(subtractor_2_out));  // open: bin, bout
  Adder adder_3 (.a(vec1_3), .b(vec2_3), .out(adder_3_out));  // open: cin, cout
  Subtractor subtractor_3 (.a(vec1_3), .b(vec2_3), .out(subtractor_3_out));  // open: bin, bout
  Adder adder_4 (.a(vec1_4), .b(vec2_4), .out(adder_4_out));  // open: cin, cout
  Subtractor subtractor_4 (.a(vec1_4), .b(vec2_4), .out(subtractor_4_out));  // open: bin, bout
  Multiplexer #(.width(8)) multiplexer_1 (.in0(adder_4_out), .in1(subtractor_4_out), .out(vec3_4), .sel(opcode));
  Multiplexer #(.width(8)) multiplexer_2 (.in0(adder_3_out), .in1(subtractor_3_out), .out(vec3_3), .sel(opcode));
  Multiplexer #(.width(8)) multiplexer_3 (.in0(adder_2_out), .in1(subtractor_2_out), .out(vec3_2), .sel(opcode));
  Multiplexer #(.width(8)) multiplexer_4 (.in0(adder_1_out), .in1(subtractor_1_out), .out(vec3_1), .sel(opcode));
endmodule
