// Logisim project RISC_I.circ as structural Verilog: 5 circuits, main circuit main
module main (
);

  wire clk, rst;
  wire [3:0] decode_1_instr_sel;
  wire [4:0] alu_1_out_5, decode_1_rd, decode_1_rs1, decode_1_rs2;
  wire [11:0] pc_1_out_3;
  wire [31:0] alu_1_out_6, decode_1_op1, decode_1_op2, regfile_1_out_8, regfile_1_out_9, rom_1_data;

  Clock clock_1 (.out(clk));
  Button button_1 (.out(rst));
  PC pc_1 (.Input(clk), .in_2(rst), .out_3(pc_1_out_3));
  ROM #(.addrWidth(10), .dataWidth(32)) rom_1 (.addr(pc_1_out_3[11:2]), .data(rom_1_data));
  // Probe on regfile_1_out_8
  // Probe on regfile_1_out_9
  decode decode_1 (
    .rs1_data(regfile_1_out_8), .rs2_data(regfile_1_out_9), .instr(rom_1_data), .rs2(decode_1_rs2),
    .rd(decode_1_rd), .instr_sel(decode_1_instr_sel), .rs1(decode_1_rs1), .op2(decode_1_op2),
    .op1(decode_1_op1));
  regfile regfile_1 (
    .in_7(decode_1_rs2), .in_2(alu_1_out_5), .in_4(decode_1_rs1), .in_5(alu_1_out_6), .in_6(1'b1),
    .in_1(clk), .in_3(rst), .out_8(regfile_1_out_8), .out_9(regfile_1_out_9));
  alu alu_1 (
    .in_1(decode_1_op1), .in_2(decode_1_op2), .in_3(decode_1_instr_sel), .in_4(decode_1_rd),
    .out_5(alu_1_out_5), .out_6(alu_1_out_6));

  // Notes on the sheet:
  //   contents of rom_1 (hex, n*v repeats v):
  //   1700e13 3900e93 1ce8f33
endmodule

module decode (
  input  [31:0] instr,
  input  [31:0] rs1_data,
  input  [31:0] rs2_data,
  output [4:0] rs1,
  output [31:0] op1,
  output [4:0] rs2,
  output [31:0] op2,
  output [4:0] rd,
  output [3:0] instr_sel
);

  wire add, andand, exclusive_or, i_sel, I_type, IR_type, op_sel, oror, R_type, shift_left_logical,
       shift_right_ari, shift_right_logical, slt, sltu, sub;
  wire [31:0] bit_extender_1_out, bit_extender_2_out, i_imm;

  Priority_Encoder #(.select(1)) priority_encoder_1 (
    .in0(I_type), .in1(R_type), .out(op_sel));  // open: gs, en_out, en_in
  // Probe on instr[11:7]
  assign bit_extender_1_out = {{20{instr[31]}}, instr[31:20]};  // Bit_Extender bit_extender_1
  Multiplexer #(.width(32)) multiplexer_1 (
    .in0(bit_extender_1_out), .in1(bit_extender_2_out), .out(i_imm), .sel(i_sel));
  assign bit_extender_2_out = {{27{instr[24]}}, instr[24:20]};  // Bit_Extender bit_extender_2
  and and_1 (R_type, ~instr[6], instr[5], instr[4], ~instr[3], ~instr[2]);  // AND_Gate
  and and_2 (I_type, ~instr[6], ~instr[5], instr[4], ~instr[3], ~instr[2]);  // AND_Gate
  // Probe on instr[19:15]
  // Probe on i_imm
  // Probe on instr[24:20]
  or or_1 (IR_type, R_type, I_type);
  and and_3 (i_sel, instr[12], ~instr[13]);  // AND_Gate
  and and_4 (add, IR_type, ~instr[30], ~instr[14], ~instr[13], ~instr[12]);  // AND_Gate
  and and_5 (sub, R_type, instr[30], ~instr[14], ~instr[13], ~instr[12]);  // AND_Gate
  and and_6 (shift_left_logical, IR_type, ~instr[14], ~instr[13], instr[12]);  // AND_Gate
  and and_7 (slt, IR_type, ~instr[14], instr[13], ~instr[12]);  // AND_Gate
  and and_8 (sltu, IR_type, ~instr[14], instr[13], instr[12]);  // AND_Gate
  and and_9 (exclusive_or, IR_type, instr[14], ~instr[13], ~instr[12]);  // AND_Gate
  and and_10 (shift_right_logical, IR_type, ~instr[30], instr[14], ~instr[13], instr[12]);  // AND_Gate
  and and_11 (shift_right_ari, IR_type, instr[30], instr[14], ~instr[13], instr[12]);  // AND_Gate
  and and_12 (oror, IR_type, instr[14], instr[13], ~instr[12]);  // AND_Gate
  and and_13 (andand, IR_type, instr[14], instr[13], instr[12]);
  Multiplexer #(.width(32)) multiplexer_2 (.in0(i_imm), .in1(rs2_data), .out(op2), .sel(op_sel));
  Priority_Encoder #(.select(4)) priority_encoder_2 (
    .in0(add), .in1(sub), .in2(shift_left_logical), .in3(slt), .in4(sltu), .in5(exclusive_or),
    .in6(shift_right_logical), .in7(shift_right_ari), .in8(oror), .in9(andand), .in10(1'b0), .in11(1'b0),
    .in12(1'b0), .in13(1'b0), .in14(1'b0), .in15(1'b0), .out(instr_sel));  // open: gs, en_out, en_in

  assign op1 = rs1_data;
  assign rd = instr[11:7];
  assign rs1 = instr[19:15];
  assign rs2 = instr[24:20];

  // Other names for the same wires on the sheet: opcode[6:0] = instr[6:0]; funct3[2:0] = instr[14:12];
  //   funct7[6:0] = instr[31:25]; flag = instr[30]

  // Notes on the sheet:
  //   Input
  //   Output
endmodule

module PC (
  input  Input,
  input  in_2,
  output [11:0] out_3
);

  wire [11:0] adder_1_out;

  Adder #(.width(12)) adder_1 (.a(out_3), .b(12'h4), .out(adder_1_out));  // open: cin, cout
  Register #(.width(12)) register_1 (.D(adder_1_out), .clk(Input), .Q(out_3), .clr(in_2));  // open: en

  // Other names for the same wires on the sheet: clk = Input; instr_addr[11:0] = out_3; rst = in_2

  // Notes on the sheet:
  //   Output
endmodule

module regfile (
  input  in_1,
  input  [4:0] in_2,
  input  in_3,
  input  [4:0] in_4,
  input  [31:0] in_5,
  input  in_6,
  input  [4:0] in_7,
  output [31:0] out_8,
  output [31:0] out_9
);

  wire en0, en1, en2, en3, en4, en5, en6, en7, en8, en9, en10, en11, en12, en13, en14, en15, en16, en17,
       en18, en19, en20, en21, en22, en23, en24, en25, en26, en27, en28, en29, en30, en31;
  wire [31:0] din0, din1, din2, din3, din4, din5, din6, din7, din8, din9, din10, din11, din12, din13, din14,
       din15, din16, din17, din18, din19, din20, din21, din22, din23, din24, din25, din26, din27, din28,
       din29, din30, din31, dout0, dout1, dout2, dout3, dout4, dout5, dout6, dout7, dout8, dout9, dout10,
       dout11, dout12, dout13, dout14, dout15, dout16, dout17, dout18, dout19, dout20, dout21, dout22,
       dout23, dout24, dout25, dout26, dout27, dout28, dout29, dout30, dout31;

  Register #(.width(32)) register_1 (.D({32{1'b0}}), .en(en0), .clk(in_1), .Q(dout0), .clr(in_3));
  Register #(.width(32)) register_2 (.D(din4), .en(en4), .clk(in_1), .Q(dout4), .clr(in_3));
  Register #(.width(32)) register_3 (.D(din8), .en(en8), .clk(in_1), .Q(dout8), .clr(in_3));
  Register #(.width(32)) register_4 (.D(din12), .en(en12), .clk(in_1), .Q(dout12), .clr(in_3));
  Register #(.width(32)) register_5 (.D(din16), .en(en16), .clk(in_1), .Q(dout16), .clr(in_3));
  Register #(.width(32)) register_6 (.D(din20), .en(en20), .clk(in_1), .Q(dout20), .clr(in_3));
  Register #(.width(32)) register_7 (.D(din24), .en(en24), .clk(in_1), .Q(dout24), .clr(in_3));
  Register #(.width(32)) register_8 (.D(din28), .en(en28), .clk(in_1), .Q(dout28), .clr(in_3));
  // Probe on dout28
  Register #(.width(32)) register_9 (.D(din1), .en(en1), .clk(in_1), .Q(dout1), .clr(in_3));
  Register #(.width(32)) register_10 (.D(din5), .en(en5), .clk(in_1), .Q(dout5), .clr(in_3));
  Register #(.width(32)) register_11 (.D(din9), .en(en9), .clk(in_1), .Q(dout9), .clr(in_3));
  Register #(.width(32)) register_12 (.D(din13), .en(en13), .clk(in_1), .Q(dout13), .clr(in_3));
  Register #(.width(32)) register_13 (.D(din17), .en(en17), .clk(in_1), .Q(dout17), .clr(in_3));
  Register #(.width(32)) register_14 (.D(din21), .en(en21), .clk(in_1), .Q(dout21), .clr(in_3));
  Register #(.width(32)) register_15 (.D(din25), .en(en25), .clk(in_1), .Q(dout25), .clr(in_3));
  Register #(.width(32)) register_16 (.D(din29), .en(en29), .clk(in_1), .Q(dout29), .clr(in_3));
  // Probe on dout29
  Register #(.width(32)) register_17 (.D(din2), .en(en2), .clk(in_1), .Q(dout2), .clr(in_3));
  Register #(.width(32)) register_18 (.D(din6), .en(en6), .clk(in_1), .Q(dout6), .clr(in_3));
  Register #(.width(32)) register_19 (.D(din10), .en(en10), .clk(in_1), .Q(dout10), .clr(in_3));
  Register #(.width(32)) register_20 (.D(din14), .en(en14), .clk(in_1), .Q(dout14), .clr(in_3));
  Register #(.width(32)) register_21 (.D(din18), .en(en18), .clk(in_1), .Q(dout18), .clr(in_3));
  Register #(.width(32)) register_22 (.D(din22), .en(en22), .clk(in_1), .Q(dout22), .clr(in_3));
  Register #(.width(32)) register_23 (.D(din26), .en(en26), .clk(in_1), .Q(dout26), .clr(in_3));
  Register #(.width(32)) register_24 (.D(din30), .en(en30), .clk(in_1), .Q(dout30), .clr(in_3));
  // Probe on dout30
  Register #(.width(32)) register_25 (.D(din3), .en(en3), .clk(in_1), .Q(dout3), .clr(in_3));
  Register #(.width(32)) register_26 (.D(din7), .en(en7), .clk(in_1), .Q(dout7), .clr(in_3));
  Register #(.width(32)) register_27 (.D(din11), .en(en11), .clk(in_1), .Q(dout11), .clr(in_3));
  Register #(.width(32)) register_28 (.D(din15), .en(en15), .clk(in_1), .Q(dout15), .clr(in_3));
  Register #(.width(32)) register_29 (.D(din19), .en(en19), .clk(in_1), .Q(dout19), .clr(in_3));
  Register #(.width(32)) register_30 (.D(din23), .en(en23), .clk(in_1), .Q(dout23), .clr(in_3));
  Register #(.width(32)) register_31 (.D(din27), .en(en27), .clk(in_1), .Q(dout27), .clr(in_3));
  Register #(.width(32)) register_32 (.D(din31), .en(en31), .clk(in_1), .Q(dout31), .clr(in_3));
  Demultiplexer #(.select(5), .width(32)) demultiplexer_1 (
    .out0(din0), .out1(din1), .out2(din2), .out3(din3), .out4(din4), .out5(din5), .out6(din6), .out7(din7),
    .out8(din8), .out9(din9), .out10(din10), .out11(din11), .out12(din12), .out13(din13), .out14(din14),
    .out15(din15), .out16(din16), .out17(din17), .out18(din18), .out19(din19), .out20(din20), .out21(din21),
    .out22(din22), .out23(din23), .out24(din24), .out25(din25), .out26(din26), .out27(din27), .out28(din28),
    .out29(din29), .out30(din30), .out31(din31), .in(in_5), .sel(in_2));
  Demultiplexer #(.select(5)) demultiplexer_2 (
    .out0(en0), .out1(en1), .out2(en2), .out3(en3), .out4(en4), .out5(en5), .out6(en6), .out7(en7),
    .out8(en8), .out9(en9), .out10(en10), .out11(en11), .out12(en12), .out13(en13), .out14(en14),
    .out15(en15), .out16(en16), .out17(en17), .out18(en18), .out19(en19), .out20(en20), .out21(en21),
    .out22(en22), .out23(en23), .out24(en24), .out25(en25), .out26(en26), .out27(en27), .out28(en28),
    .out29(en29), .out30(en30), .out31(en31), .in(in_6), .sel(in_2));
  Multiplexer #(.select(5), .width(32)) multiplexer_1 (
    .in0(dout0), .in1(dout1), .in2(dout2), .in3(dout3), .in4(dout4), .in5(dout5), .in6(dout6), .in7(dout7),
    .in8(dout8), .in9(dout9), .in10(dout10), .in11(dout11), .in12(dout12), .in13(dout13), .in14(dout14),
    .in15(dout15), .in16(dout16), .in17(dout17), .in18(dout18), .in19(dout19), .in20(dout20), .in21(dout21),
    .in22(dout22), .in23(dout23), .in24(dout24), .in25(dout25), .in26(dout26), .in27(dout27), .in28(dout28),
    .in29(dout29), .in30(dout30), .in31(dout31), .out(out_8), .sel(in_4));
  Multiplexer #(.select(5), .width(32)) multiplexer_2 (
    .in0(dout0), .in1(dout1), .in2(dout2), .in3(dout3), .in4(dout4), .in5(dout5), .in6(dout6), .in7(dout7),
    .in8(dout8), .in9(dout9), .in10(dout10), .in11(dout11), .in12(dout12), .in13(dout13), .in14(dout14),
    .in15(dout15), .in16(dout16), .in17(dout17), .in18(dout18), .in19(dout19), .in20(dout20), .in21(dout21),
    .in22(dout22), .in23(dout23), .in24(dout24), .in25(dout25), .in26(dout26), .in27(dout27), .in28(dout28),
    .in29(dout29), .in30(dout30), .in31(dout31), .out(out_9), .sel(in_7));

  // Other names for the same wires on the sheet: clk = in_1; din[31:0] = in_5; en = in_6; rs1_addr[4:0] = in_4;
  //   rs1_data[31:0] = out_8; rs2_addr[4:0] = in_7; rs2_data[31:0] = out_9; rst = in_3; wr_addr[4:0] = in_2
endmodule

module alu (
  input  [31:0] in_1,
  input  [31:0] in_2,
  input  [3:0] in_3,
  input  [4:0] in_4,
  output [4:0] out_5,
  output [31:0] out_6
);

  wire [0:0] comparator_1_lt, comparator_2_lt;
  wire [31:0] adder_1_out, and_1_out, or_1_out, shifter_1_out, shifter_2_out, shifter_3_out,
       subtractor_1_out, xor_1_out;

  Adder #(.width(32)) adder_1 (.a(in_1), .b(in_2), .out(adder_1_out));  // open: cin, cout
  Subtractor #(.width(32)) subtractor_1 (.a(in_1), .b(in_2), .out(subtractor_1_out));  // open: bin, bout
  Shifter #(.width(32)) shifter_1 (.in(in_1), .\dist (in_2[4:0]), .out(shifter_1_out));
  Comparator #(.width(32)) comparator_1 (.a(in_1), .b(in_2), .lt(comparator_1_lt[0]));  // open: gt, eq
  Comparator #(.width(32)) comparator_2 (.a(in_1), .b(in_2), .lt(comparator_2_lt[0]));  // open: gt, eq
  assign xor_1_out = in_1 ^ in_2;  // XOR_Gate xor_1, 32 bits wide
  Shifter #(.shift("lr"), .width(32)) shifter_2 (.in(in_1), .\dist (in_2[4:0]), .out(shifter_2_out));
  Shifter #(.shift("ar"), .width(32)) shifter_3 (.in(in_1), .\dist (in_2[4:0]), .out(shifter_3_out));
  assign or_1_out = in_1 | in_2;  // OR_Gate or_1, 32 bits wide
  assign and_1_out = in_1 & in_2;  // AND_Gate and_1, 32 bits wide
  Multiplexer #(.select(4), .width(32)) multiplexer_1 (
    .in0(adder_1_out), .in1(subtractor_1_out), .in2(shifter_1_out), .in3({{31{1'b0}}, comparator_1_lt[0]}),
    .in4({{31{1'b0}}, comparator_2_lt[0]}), .in5(xor_1_out), .in6(shifter_2_out), .in7(shifter_3_out),
    .in8(or_1_out), .in9(and_1_out), .in10({32{1'b0}}), .in11({32{1'b0}}), .in12({32{1'b0}}),
    .in13({32{1'b0}}), .in14({32{1'b0}}), .in15({32{1'b0}}), .out(out_6), .sel(in_3));

  assign out_5 = in_4;

  // Other names for the same wires on the sheet: instr_sel[3:0] = in_3; op1[31:0] = in_1; op2[31:0] = in_2;
  //   rd[4:0] = in_4; rd_addr[4:0] = in_4; rd_data[31:0] = out_6

  // Notes on the sheet:
  //   Input
  //   Output
endmodule
